// Logisim project Lab1real.circ as structural Verilog: 3 circuits, main circuit main
module main (
);


  // Notes on the sheet:
  //   Lab 1
  //   Gonzalo Palenzuela
  //   Sophia RIce
endmodule

module part2 (
  input  A,
  input  B,
  input  A_s,
  input  B_s,
  input  V,
  input  W,
  input  X,
  input  Y,
  input  X_S,
  input  V_S,
  input  W_S,
  output F,
  output F_S,
  output Z,
  output Z_S
);

  wire and_1_out, and_2_out, and_3_out, and_4_out, and_5_out, and_6_out, not_1_out, not_2_out, not_3_out,
       not_4_out, not_5_out;

  not not_1 (not_1_out, V);
  not not_2 (not_2_out, V_S);
  not not_3 (not_3_out, B);
  not not_4 (not_4_out, A);
  or or_1 (F_S, A_s, B_s);
  and and_1 (and_1_out, not_1_out, W);
  and and_2 (and_2_out, not_2_out, W_S);
  and and_3 (and_3_out, A, B);
  and and_4 (and_4_out, A, not_3_out);
  and and_5 (and_5_out, not_4_out, B);
  not not_5 (not_5_out, Y);
  and and_6 (and_6_out, not_5_out, and_1_out);
  or or_2 (Z_S, X_S, and_2_out);
  or or_3 (F, and_3_out, and_4_out, and_5_out);
  or or_4 (Z, and_1_out, X, and_6_out);

  // Notes on the sheet:
  //   Lab 1, Part 2
endmodule

module part3c (
  input  D,
  input  W,
  input  M,
  output A,
  output S
);

  wire not_1_out, not_2_out, or_1_out;

  not not_1 (not_1_out, D);
  not not_2 (not_2_out, W);
  or or_1 (or_1_out, not_1_out, not_2_out);
  and and_1 (A, or_1_out, M);
  or or_2 (S, not_1_out, not_2_out, M);

  // Notes on the sheet:
  //   Lab 1, part 3c
endmodule
